// Logisim project 3a_LASACS_7Segment.circ as structural Verilog: 1 circuit, main circuit main
module main (
  input  x,
  input  y,
  input  z
);

  wire and_1_out, and_2_out, and_3_out, and_4_out, and_5_out, and_6_out, not_1_out, not_2_out, not_3_out,
       or_1_out, or_2_out, or_3_out, or_4_out, or_5_out, or_6_out;

  not not_1 (not_1_out, x);
  not not_2 (not_2_out, y);
  not not_3 (not_3_out, z);
  and and_1 (and_1_out, not_1_out, not_2_out, not_3_out);
  and and_2 (and_2_out, not_1_out, not_2_out, z);
  and and_3 (and_3_out, not_1_out, y, not_3_out);
  and and_4 (and_4_out, not_1_out, y, z);
  and and_5 (and_5_out, x, not_2_out, not_3_out);
  and and_6 (and_6_out, x, not_2_out, z);
  or or_1 (or_1_out, and_2_out, and_3_out, and_4_out, and_5_out, and_6_out);
  or or_2 (or_2_out, and_2_out, and_4_out);
  or or_3 (or_3_out, and_2_out, and_3_out, and_4_out, and_6_out);
  or or_4 (or_4_out, and_1_out, and_3_out, and_5_out, and_6_out);
  or or_5 (or_5_out, and_1_out, and_2_out, and_4_out, and_5_out);
  or or_6 (or_6_out, and_2_out, and_3_out, and_4_out, and_6_out);
  _7_Segment_Display u_7_segment_display_1 (
    .g(or_6_out), .f(1'b1), .a(or_1_out), .b(or_2_out), .e(or_5_out), .d(or_4_out), .c(or_3_out), .dp(1'b0));
endmodule
