// Logisim project 3a_LASACS_7Segment_Partially_Simplified.circ as structural Verilog: 2 circuits, main circuit Partially_Simplified
module Partially_Simplified (
  input  x,
  input  y,
  input  z
);

  wire A_out, and_1_out, and_2_out, B_out, CG_out, D_out, E_out, not_1_out, not_2_out, not_3_out;

  not not_1 (not_1_out, x);
  not not_2 (not_2_out, y);
  not not_3 (not_3_out, z);
  and and_1 (and_1_out, not_1_out, z);
  and and_2 (and_2_out, not_2_out, not_3_out);
  or A (A_out, x, y, z);
  and B (B_out, not_1_out, z);
  or CG (CG_out, y, z);
  or D (D_out, not_3_out, x);
  or E (E_out, and_1_out, and_2_out);
  _7_Segment_Display u_7_segment_display_1 (
    .g(CG_out), .f(1'b1), .a(A_out), .b(B_out), .e(E_out), .d(D_out), .c(CG_out), .dp(1'b0));

  // Notes on the sheet:
  //   50 transistors
endmodule

module DeMorgans (
  input  x,
  input  y,
  input  z
);

  wire A_out, B_out, CG_out, D_out, E_out, nand_1_out, nand_2_out, not_1_out, not_2_out, not_3_out;

  not not_1 (not_1_out, x);
  not not_2 (not_2_out, y);
  not not_3 (not_3_out, z);
  nand nand_1 (nand_1_out, not_1_out, z);
  nand nand_2 (nand_2_out, not_2_out, not_3_out);
  nand A (A_out, not_1_out, not_2_out, not_3_out);
  nor B (B_out, x, not_3_out);
  nand CG (CG_out, not_2_out, not_3_out);
  nand D (D_out, z, not_1_out);
  nand E (E_out, nand_1_out, nand_2_out);
  _7_Segment_Display u_7_segment_display_1 (
    .g(CG_out), .f(1'b1), .a(A_out), .b(B_out), .e(E_out), .d(D_out), .c(CG_out), .dp(1'b0));

  // Notes on the sheet:
  //   36 transistors
endmodule
