// Logisim project 3b_XOR.circ as structural Verilog
module MyXOR (
  input  in_1,
  input  in_2,
  output out_3
);

  wire and_1_out, and_2_out, not_1_out, not_2_out;

  not not_1 (not_1_out, in_1);
  not not_2 (not_2_out, in_2);
  and and_1 (and_1_out, not_1_out, in_2);
  and and_2 (and_2_out, in_1, not_2_out);
  or or_1 (out_3, and_1_out, and_2_out);
endmodule

module MyXORCircuit (
  input  a,
  input  b,
  input  c,
  output y
);

  wire myxor_1_out_3;

  MyXOR myxor_1 (.in_1(a), .in_2(b), .out_3(myxor_1_out_3));
  MyXOR myxor_2 (.in_1(myxor_1_out_3), .in_2(c), .out_3(y));
endmodule
