// Logisim project 4bit_7_Segment.circ as structural Verilog: 3 circuits, main circuit Simplified
module Simplified (
  input  w,
  input  x,
  input  y,
  input  z
);

  wire A_out, and_1_out, and_2_out, and_3_out, and_4_out, and_5_out, and_6_out, and_7_out, and_8_out,
       and_9_out, and_10_out, B_out, C_out, D_out, E_out, F_out, G_out, not_1_out, not_2_out, not_3_out,
       not_4_out;

  not not_1 (not_1_out, w);
  not not_2 (not_2_out, x);
  not not_3 (not_3_out, y);
  not not_4 (not_4_out, z);
  and and_1 (and_1_out, not_1_out, not_2_out, not_3_out, z);
  and and_2 (and_2_out, x, not_3_out, not_4_out);
  and and_3 (and_3_out, x, not_3_out, z);
  and and_4 (and_4_out, x, y, not_4_out);
  and C (C_out, not_2_out, y, not_4_out);
  and and_5 (and_5_out, x, y, z);
  and and_6 (and_6_out, x, not_3_out);
  and and_7 (and_7_out, not_1_out, not_2_out, z);
  and and_8 (and_8_out, not_2_out, y);
  and and_9 (and_9_out, y, z);
  and and_10 (and_10_out, not_1_out, not_2_out, not_3_out);
  or A (A_out, and_1_out, and_2_out);
  or B (B_out, and_3_out, and_4_out);
  or D (D_out, and_2_out, and_5_out, and_1_out);
  or E (E_out, and_6_out, z);
  or F (F_out, and_7_out, and_8_out, and_9_out);
  or G (G_out, and_5_out, and_10_out);
  _7_Segment_Display #(.active("false")) u_7_segment_display_1 (
    .g(G_out), .f(F_out), .a(A_out), .b(B_out), .e(E_out), .d(D_out), .c(C_out), .dp(1'b1));
endmodule

module Optimized (
  input  w,
  input  x,
  input  y,
  input  z
);

  wire A_out, B_out, C_out, D_out, E_out, F_out, G_out, nand_1_out, nand_2_out, nand_3_out, nand_4_out,
       nand_5_out, nand_6_out, nand_7_out, nand_8_out, nand_9_out, nand_10_out, not_1_out, not_2_out,
       not_3_out, not_4_out;

  not not_1 (not_1_out, w);
  not not_2 (not_2_out, x);
  not not_3 (not_3_out, y);
  not not_4 (not_4_out, z);
  nand nand_1 (nand_1_out, not_1_out, not_2_out, not_3_out, z);
  nand nand_2 (nand_2_out, x, not_3_out, not_4_out);
  nand nand_3 (nand_3_out, x, not_3_out, z);
  nand nand_4 (nand_4_out, x, y, not_4_out);
  nor C (C_out, x, not_3_out, z);
  nand nand_5 (nand_5_out, x, y, z);
  nand nand_6 (nand_6_out, x, not_3_out);
  nand nand_7 (nand_7_out, not_1_out, not_2_out, z);
  nand nand_8 (nand_8_out, not_2_out, y);
  nand nand_9 (nand_9_out, y, z);
  nand nand_10 (nand_10_out, not_1_out, not_2_out, not_3_out);
  nand A (A_out, nand_1_out, nand_2_out);
  nand B (B_out, nand_3_out, nand_4_out);
  nand D (D_out, nand_2_out, nand_5_out, nand_1_out);
  nand E (E_out, nand_6_out, not_4_out);
  nand F (F_out, nand_7_out, nand_8_out, nand_9_out);
  nand G (G_out, nand_5_out, nand_10_out);
  _7_Segment_Display #(.active("false")) u_7_segment_display_1 (
    .g(G_out), .f(F_out), .a(A_out), .b(B_out), .e(E_out), .d(D_out), .c(C_out), .dp(1'b1));
endmodule

module GatesRemoved (
  input  w,
  input  x,
  input  y,
  input  z
);

  wire A_out, B_out, C_out, D_out, E_out, F_out, G_out, nand_1_out, nand_2_out, nand_3_out, nand_4_out,
       nand_5_out, nand_6_out, nand_7_out, not_1_out, not_2_out, not_3_out, not_4_out;

  not not_1 (not_1_out, w);
  not not_2 (not_2_out, x);
  not not_3 (not_3_out, y);
  not not_4 (not_4_out, z);
  nand nand_1 (nand_1_out, not_1_out, not_2_out, not_3_out, z);
  nand nand_2 (nand_2_out, x, not_3_out, not_4_out);
  nand nand_3 (nand_3_out, x, not_3_out, z);
  nand nand_4 (nand_4_out, x, y, not_4_out);
  nor C (C_out, x, not_3_out, z);
  nand nand_5 (nand_5_out, x, y, z);
  nand nand_6 (nand_6_out, not_2_out, y);
  nand nand_7 (nand_7_out, not_1_out, not_2_out, not_3_out);
  nand A (A_out, nand_1_out, nand_2_out);
  nand B (B_out, nand_3_out, nand_4_out);
  nand F (F_out, nand_1_out, nand_5_out, nand_6_out);
  nand D (D_out, nand_2_out, nand_5_out, nand_1_out);
  nand E (E_out, nand_2_out, not_4_out);
  nand G (G_out, nand_5_out, nand_7_out);
  _7_Segment_Display #(.active("false")) u_7_segment_display_1 (
    .g(G_out), .f(F_out), .a(A_out), .b(B_out), .e(E_out), .d(D_out), .c(C_out), .dp(1'b1));
endmodule
