// Logisim project Adder_Subtract.circ as structural Verilog: 3 circuits, main circuit LogisimBasedAddSubtract
module LogisimBasedAddSubtract (
  input  OP,
  input  [15:0] A,
  input  [15:0] B,
  output [15:0] Sum,
  output Overflow
);

  wire and_1_out, and_2_out, nor_1_out, nor_2_out, nor_3_out, or_1_out;
  wire [15:0] multiplexer_1_out, not_1_out;

  Multiplexer #(.width(16)) multiplexer_1 (.in0(B), .in1(not_1_out), .out(multiplexer_1_out), .sel(OP));
  assign not_1_out = ~B;  // NOT_Gate not_1, 16 bits wide
  Adder #(.width(16)) adder_1 (.a(A), .b(multiplexer_1_out), .out(Sum), .cin(OP));  // open: cout
  and and_1 (and_1_out, multiplexer_1_out[15], A[15]);
  nor nor_1 (nor_1_out, multiplexer_1_out[15], A[15]);
  and and_2 (and_2_out, Sum[15], A[15]);
  nor nor_2 (nor_2_out, Sum[15], A[15]);
  or or_1 (or_1_out, and_1_out, nor_1_out);
  nor nor_3 (nor_3_out, and_2_out, nor_2_out);
  and and_3 (Overflow, or_1_out, nor_3_out);
endmodule

module CSBasedAddSubtract (
  input  OP,
  input  [15:0] A,
  input  [15:0] B,
  output [15:0] Sum,
  output Overflow
);

  wire and_1_out, and_2_out, nor_1_out, nor_2_out, nor_3_out, or_1_out;
  wire [15:0] multiplexer_1_out, not_1_out;

  Multiplexer #(.width(16)) multiplexer_1 (.in0(B), .in1(not_1_out), .out(multiplexer_1_out), .sel(OP));
  assign not_1_out = ~B;  // NOT_Gate not_1, 16 bits wide
  CarrySelect16BitFullAdder carryselect16bitfulladder_1 (
    .Cin(OP), .A(A), .B(multiplexer_1_out), .s(Sum));  // open: Cout
  and and_1 (and_1_out, multiplexer_1_out[15], A[15]);
  nor nor_1 (nor_1_out, multiplexer_1_out[15], A[15]);
  and and_2 (and_2_out, Sum[15], A[15]);
  nor nor_2 (nor_2_out, Sum[15], A[15]);
  or or_1 (or_1_out, and_1_out, nor_1_out);
  nor nor_3 (nor_3_out, and_2_out, nor_2_out);
  and and_3 (Overflow, or_1_out, nor_3_out);
endmodule

module CarrySelect16BitFullAdder (
  input  [15:0] A,
  input  [15:0] B,
  input  Cin,
  output [15:0] s,
  output Cout
);

  wire carryselect8bit1_1_cout, carryselect8bit1_2_cout, carryselect8bit_1_cout, carryselect8bit_2_cout,
       multiplexer_3_out;
  wire [7:0] carryselect8bit1_1_s, carryselect8bit1_2_s, carryselect8bit_1_s, carryselect8bit_2_s;

  CarrySelect8Bit carryselect8bit_1 (.A(A[15:8]), .B(B[15:8]), .s(carryselect8bit_1_s), .Cout(carryselect8bit_1_cout));
  Multiplexer #(.width(8)) multiplexer_1 (
    .in0(carryselect8bit_1_s), .in1(carryselect8bit1_1_s), .out(s[15:8]), .sel(multiplexer_3_out));
  Multiplexer multiplexer_2 (
    .in0(carryselect8bit_1_cout), .in1(carryselect8bit1_1_cout), .out(Cout), .sel(multiplexer_3_out));
  CarrySelect8Bit1 carryselect8bit1_1 (
    .A(A[15:8]), .B(B[15:8]), .s(carryselect8bit1_1_s), .Cout(carryselect8bit1_1_cout));
  Multiplexer multiplexer_3 (
    .in0(carryselect8bit_2_cout), .in1(carryselect8bit1_2_cout), .out(multiplexer_3_out), .sel(Cin));
  CarrySelect8Bit carryselect8bit_2 (.A(A[7:0]), .B(B[7:0]), .s(carryselect8bit_2_s), .Cout(carryselect8bit_2_cout));
  CarrySelect8Bit1 carryselect8bit1_2 (
    .A(A[7:0]), .B(B[7:0]), .s(carryselect8bit1_2_s), .Cout(carryselect8bit1_2_cout));
  Multiplexer #(.width(8)) multiplexer_4 (
    .in0(carryselect8bit_2_s), .in1(carryselect8bit1_2_s), .out(s[7:0]), .sel(Cin));

  // Notes on the sheet:
  //   10.5
  //   12.25
  //   10.5
  //   10.5
  //   12.25
  //   10.5
  //   10.5
  //   10.5
  //   13
endmodule
