// Logisim project Adders.circ as structural Verilog: 12 circuits, main circuit FA0
module FA0 (
  input  a,
  input  b,
  output s,
  output c
);

  wire nor_1_out;

  nor nor_1 (nor_1_out, a, b);
  and and_1 (c, a, b);
  nor nor_2 (s, nor_1_out, c);

  // Notes on the sheet:
  //   14 transistors
  //   FA0
  //   Saffron Liu
  //   2.75
  //   1.75
endmodule

module FA1 (
  input  a,
  input  b,
  output s,
  output c
);

  wire nand_1_out;

  nand nand_1 (nand_1_out, a, b);
  or or_1 (c, a, b);
  nand nand_2 (s, nand_1_out, c);

  // Notes on the sheet:
  //   14 transistors
  //   FA1
  //   Saffron Liu
  //   2.75
  //   1.75
endmodule

module FAopt1 (
  input  A,
  input  B,
  input  Cin,
  output S,
  output Cout
);

  wire nand_1_out, nand_2_out, nor_1_out, nor_2_out, nor_3_out, not_1_out, not_2_out;

  nor nor_1 (nor_1_out, A, B);
  nand nand_1 (nand_1_out, A, B);
  not not_1 (not_1_out, nand_1_out);
  nor nor_2 (nor_2_out, nor_1_out, not_1_out);
  nand nand_2 (nand_2_out, nor_2_out, Cin);
  nor nor_3 (nor_3_out, nor_2_out, Cin);
  not not_2 (not_2_out, nand_2_out);
  nand nand_3 (Cout, nand_1_out, nand_2_out);
  nor nor_4 (S, nor_3_out, not_2_out);

  // Notes on the sheet:
  //   32 transistors
  //   FAopt1
  //   Saffron Liu
  //   If Cin < 2.75: 5.5
  //   If Cin < 2.75: 4.75
  //   If Cin > 2.75: Cin + 2
  //   If Cin > 2.75: Cin + 2.75
endmodule

module FAopt2 (
  input  A,
  input  B,
  input  Cin,
  output S,
  output Cout
);

  wire and_1_out, nand_1_out, nand_2_out, nand_3_out, nor_1_out, nor_2_out, nor_3_out, not_1_out;

  nor nor_1 (nor_1_out, A, B);
  nand nand_1 (nand_1_out, A, B);
  nand nand_2 (nand_2_out, A, Cin);
  nand nand_3 (nand_3_out, B, Cin);
  not not_1 (not_1_out, nand_1_out);
  nand nand_4 (Cout, nand_1_out, nand_2_out, nand_3_out);
  nor nor_2 (nor_2_out, nor_1_out, not_1_out);
  nor nor_3 (nor_3_out, nor_2_out, Cin);
  and and_1 (and_1_out, nor_2_out, Cin);
  nor nor_4 (S, nor_3_out, and_1_out);

  // Notes on the sheet:
  //   42 transistors
  //   Cin + 2.25
  //   FAopt2
  //   Saffron Liu
  //   If Cin < 2.75: 5.5
  //   If Cin > 2.75: Cin + 2.75
endmodule

module Ripple4Bit0 (
  input  [3:0] A,
  input  [3:0] B,
  output [3:0] S,
  output Cout
);

  wire fa0_1_c, faopt1_2_cout, faopt2_1_cout;

  FAopt1 faopt1_1 (.A(A[3]), .B(B[3]), .Cin(faopt1_2_cout), .Cout(Cout), .S(S[3]));
  FAopt1 faopt1_2 (.A(A[2]), .B(B[2]), .Cin(faopt2_1_cout), .Cout(faopt1_2_cout), .S(S[2]));
  FAopt2 faopt2_1 (.A(A[1]), .B(B[1]), .Cin(fa0_1_c), .Cout(faopt2_1_cout), .S(S[1]));
  FA0 fa0_1 (.a(A[0]), .b(B[0]), .s(S[0]), .c(fa0_1_c));

  // Notes on the sheet:
  //   8
  //   6
  //   8.75
  //   4
  //   6.75
  //   1.75
  //   2.75
  //   5.5
  //   120 transistors
  //   4-bit Ripple Carry Adder
  //   Saffron Liu
endmodule

module Ripple4Bit1 (
  input  [3:0] A,
  input  [3:0] B,
  output [3:0] S,
  output Cout
);

  wire fa1_1_c, faopt1_2_cout, faopt2_1_cout;

  FAopt1 faopt1_1 (.A(A[3]), .B(B[3]), .Cin(faopt1_2_cout), .Cout(Cout), .S(S[3]));
  FAopt1 faopt1_2 (.A(A[2]), .B(B[2]), .Cin(faopt2_1_cout), .Cout(faopt1_2_cout), .S(S[2]));
  FAopt2 faopt2_1 (.A(A[1]), .B(B[1]), .Cin(fa1_1_c), .Cout(faopt2_1_cout), .S(S[1]));
  FA1 fa1_1 (.a(A[0]), .b(B[0]), .s(S[0]), .c(fa1_1_c));

  // Notes on the sheet:
  //   8
  //   6
  //   8.75
  //   4
  //   6.75
  //   1.75
  //   2.75
  //   5.5
  //   120 transistors
  //   4-bit Ripple Carry Adder
  //   Saffron Liu
endmodule

module Ripple8Bit (
  input  [7:0] A,
  input  [7:0] B,
  output [7:0] S,
  output Cout
);

  wire fa0_1_c, faopt1_2_cout, faopt1_3_cout, faopt1_4_cout, faopt1_5_cout, faopt1_6_cout, faopt2_1_cout;

  FAopt1 faopt1_1 (.A(A[7]), .B(B[7]), .Cin(faopt1_2_cout), .Cout(Cout), .S(S[7]));
  FAopt1 faopt1_2 (.A(A[6]), .B(B[6]), .Cin(faopt1_3_cout), .Cout(faopt1_2_cout), .S(S[6]));
  FAopt1 faopt1_3 (.A(A[5]), .B(B[5]), .Cin(faopt1_4_cout), .Cout(faopt1_3_cout), .S(S[5]));
  FAopt1 faopt1_4 (.A(A[4]), .B(B[4]), .Cin(faopt1_5_cout), .Cout(faopt1_4_cout), .S(S[4]));
  FAopt1 faopt1_5 (.A(A[3]), .B(B[3]), .Cin(faopt1_6_cout), .Cout(faopt1_5_cout), .S(S[3]));
  FAopt1 faopt1_6 (.A(A[2]), .B(B[2]), .Cin(faopt2_1_cout), .Cout(faopt1_6_cout), .S(S[2]));
  FAopt2 faopt2_1 (.A(A[1]), .B(B[1]), .Cin(fa0_1_c), .Cout(faopt2_1_cout), .S(S[1]));
  FA0 fa0_1 (.a(A[0]), .b(B[0]), .s(S[0]), .c(fa0_1_c));

  // Notes on the sheet:
  //   16
  //   14
  //   16.75
  //   12
  //   14.75
  //   10
  //   12.75
  //   8
  //   10.75
  //   6
  //   8.75
  //   4
  //   6.75
  //   1.75
  //   5.5
  //   2.75
  //   248 transistors
  //   8-bit Ripple Carry Adder
  //   Saffron Liu
endmodule

module CarrySelect8Bit (
  input  [7:0] A,
  input  [7:0] B,
  output [7:0] s,
  output Cout
);

  wire mux2to1transmission_1_out_4, ripple4bit0_1_cout, ripple4bit0_2_cout, ripple4bit1_1_cout;
  wire [3:0] mux2to1inv_4bit_1_out_4, ripple4bit0_1_s, ripple4bit1_1_s;

  Ripple4Bit1 ripple4bit1_1 (.A(A[7:4]), .B(B[7:4]), .S(ripple4bit1_1_s), .Cout(ripple4bit1_1_cout));
  Mux2to1Inv_4Bit mux2to1inv_4bit_1 (
    .Cin(ripple4bit0_2_cout), .A(ripple4bit0_1_s), .B(ripple4bit1_1_s), .out_4(mux2to1inv_4bit_1_out_4));
  assign s[7:4] = ~mux2to1inv_4bit_1_out_4;  // NOT_Gate not_1, 4 bits wide
  not not_2 (Cout, mux2to1transmission_1_out_4);
  Mux2to1Transmission mux2to1transmission_1 (
    .in1(ripple4bit1_1_cout), .s(ripple4bit0_2_cout), .in0(ripple4bit0_1_cout),
    .out_4(mux2to1transmission_1_out_4));
  Ripple4Bit0 ripple4bit0_1 (.A(A[7:4]), .B(B[7:4]), .S(ripple4bit0_1_s), .Cout(ripple4bit0_1_cout));
  Ripple4Bit0 ripple4bit0_2 (.A(A[3:0]), .B(B[3:0]), .S(s[3:0]), .Cout(ripple4bit0_2_cout));

  // Notes on the sheet:
  //   8
  //   8
  //   8.75
  //   9.75
  //   9.75
  //   8
  //   8.75
  //   8.75
  //   Saffron Liu
  //   10.5
  //   10.5
  //   8-bit Carry Select Adder
endmodule

module CarrySelect8Bit1 (
  input  [7:0] A,
  input  [7:0] B,
  output [7:0] s,
  output Cout
);

  wire mux2to1transmission_1_out_4, ripple4bit0_1_cout, ripple4bit1_1_cout, ripple4bit1_2_cout;
  wire [3:0] mux2to1inv_4bit_1_out_4, ripple4bit0_1_s, ripple4bit1_1_s;

  Ripple4Bit1 ripple4bit1_1 (.A(A[7:4]), .B(B[7:4]), .S(ripple4bit1_1_s), .Cout(ripple4bit1_1_cout));
  Mux2to1Inv_4Bit mux2to1inv_4bit_1 (
    .Cin(ripple4bit1_2_cout), .A(ripple4bit0_1_s), .B(ripple4bit1_1_s), .out_4(mux2to1inv_4bit_1_out_4));
  assign s[7:4] = ~mux2to1inv_4bit_1_out_4;  // NOT_Gate not_1, 4 bits wide
  not not_2 (Cout, mux2to1transmission_1_out_4);
  Mux2to1Transmission mux2to1transmission_1 (
    .in1(ripple4bit1_1_cout), .s(ripple4bit1_2_cout), .in0(ripple4bit0_1_cout),
    .out_4(mux2to1transmission_1_out_4));
  Ripple4Bit0 ripple4bit0_1 (.A(A[7:4]), .B(B[7:4]), .S(ripple4bit0_1_s), .Cout(ripple4bit0_1_cout));
  Ripple4Bit1 ripple4bit1_2 (.A(A[3:0]), .B(B[3:0]), .S(s[3:0]), .Cout(ripple4bit1_2_cout));

  // Notes on the sheet:
  //   8
  //   8
  //   8.75
  //   9.75
  //   9.75
  //   8
  //   8.75
  //   8.75
  //   Saffron Liu
  //   10.5
  //   10.5
  //   8-bit Carry Select Adder
endmodule

module CarrySelect16Bit (
  input  [15:0] A,
  input  [15:0] B,
  output [15:0] s,
  output Cout
);

  wire carryselect8bit1_1_cout, carryselect8bit_1_cout, carryselect8bit_2_cout, mux2to1transmission_1_out_4;
  wire [7:0] carryselect8bit1_1_s, carryselect8bit_1_s, mux2to1inv_8bit_1_out_4;

  CarrySelect8Bit1 carryselect8bit1_1 (
    .A(A[15:8]), .B(B[15:8]), .s(carryselect8bit1_1_s), .Cout(carryselect8bit1_1_cout));
  Mux2to1Transmission mux2to1transmission_1 (
    .in1(carryselect8bit1_1_cout), .s(carryselect8bit_2_cout), .in0(carryselect8bit_1_cout),
    .out_4(mux2to1transmission_1_out_4));
  Mux2to1Inv_8Bit mux2to1inv_8bit_1 (
    .B(carryselect8bit1_1_s), .A(carryselect8bit_1_s), .Cin(carryselect8bit_2_cout),
    .out_4(mux2to1inv_8bit_1_out_4));
  assign s[15:8] = ~mux2to1inv_8bit_1_out_4;  // NOT_Gate not_1, 8 bits wide
  not not_2 (Cout, mux2to1transmission_1_out_4);
  CarrySelect8Bit carryselect8bit_1 (.A(A[15:8]), .B(B[15:8]), .s(carryselect8bit_1_s), .Cout(carryselect8bit_1_cout));
  CarrySelect8Bit carryselect8bit_2 (.A(A[7:0]), .B(B[7:0]), .s(s[7:0]), .Cout(carryselect8bit_2_cout));

  // Notes on the sheet:
  //   10.5
  //   12.25
  //   10.5
  //   10.5
  //   12.25
  //   10.5
  //   10.5
  //   10.5
  //   13
  //   13
endmodule

module LookaheadAdderv3 (
  input  P0,
  input  P1,
  input  P2,
  input  P3,
  input  G3,
  input  G2,
  input  G1,
  input  G0,
  input  C0,
  output C4
);

  wire aoi21_1_out_4, nand_1_out, nand_2_out, nand_3_out, nand_4_out, nor_1_out, nor_2_out, nor_3_out,
       nor_4_out, not_1_out, not_2_out, not_3_out, not_4_out;

  nand nand_1 (nand_1_out, P3, G2);
  nand nand_2 (nand_2_out, P3, P2, G1);
  nand nand_3 (nand_3_out, P3, P2, P1);
  not not_1 (not_1_out, nand_1_out);
  not not_2 (not_2_out, nand_2_out);
  not not_3 (not_3_out, G0);
  not not_4 (not_4_out, P0);
  nor nor_1 (nor_1_out, nand_3_out, not_3_out);
  nor nor_2 (nor_2_out, nand_3_out, not_4_out);
  nor nor_3 (nor_3_out, G3, not_1_out);
  nor nor_4 (nor_4_out, not_2_out, nor_1_out);
  nand nand_4 (nand_4_out, nor_3_out, nor_4_out);
  not not_5 (C4, aoi21_1_out_4);
  AOI21 aoi21_1 (.C(C0), .A(nand_4_out), .B(nor_2_out), .out_4(aoi21_1_out_4));
endmodule

module AOI21 (
  input  A,
  input  B,
  input  C,
  output out_4
);

  wire transistor_1_out, transistor_6_out;

  Transistor transistor_1 (.in(1'b1), .out(transistor_1_out), .gate(C));
  Transistor transistor_2 (.in(transistor_1_out), .out(out_4), .gate(A));
  Transistor #(.\type ("n")) transistor_3 (.in(1'b0), .out(out_4), .gate(A));
  Transistor transistor_4 (.in(1'b1), .out(transistor_1_out), .gate(B));
  Transistor #(.\type ("n")) transistor_5 (.in(transistor_6_out), .out(out_4), .gate(B));
  Transistor #(.\type ("n")) transistor_6 (.in(1'b0), .out(transistor_6_out), .gate(C));
endmodule
