// Logisim project LALU.circ as structural Verilog: 6 circuits, main circuit main
module main (
  input  rst,
  output [15:0] out_2,
  output [15:0] out_3,
  output [15:0] out_4,
  output [15:0] cycle,
  output [15:0] out_6,
  output [15:0] out_7
);

  wire and_1_out, and_2_out, and_3_out, and_4_out, clk, halt, jumpEnable, overflow, register_1_q,
       regwe_1_reg0we, regwe_1_reg1we, regwe_1_reg2we, regwe_1_reg3we, rW, sub;
  wire [1:0] Rd, Rs;
  wire [3:0] op;
  wire [5:0] jumpTarg, programcounter_1_pc;
  wire [7:0] instructionRegister_q, ram_2_dout;
  wire [15:0] ld, multiplexer_1_out, multiplexer_2_out, selRd, selRs, sum;

  Clock clock_1 (.out(clk));
  RAM #(.asyncread("true"), .dataWidth(16), .trigger("falling")) ram_1 (
    .addr(selRs[7:0]), .we(and_1_out), .clk(clk), .din(selRd), .dout(ld));  // open: oe
  and and_1 (and_1_out, op[3], ~op[2], op[1]);  // AND_Gate
  programCounter programcounter_1 (
    .jumpTarg(jumpTarg), .jumpEnable(jumpEnable), .clk(clk), .rst(rst), .pc(programcounter_1_pc));
  cycleCounter cyclecounter_1 (.halt(halt), .clk(clk), .rst(rst), .out_4(cycle));
  RAM #(.addrWidth(6), .asyncread("true"), .trigger("falling")) ram_2 (
    .addr(programcounter_1_pc), .we(1'b0), .oe(1'b1), .clk(clk), .dout(ram_2_dout));  // open: din
  Register instructionRegister (.D(ram_2_dout), .en(1'b1), .clk(clk), .Q(instructionRegister_q), .clr(rst));
  srcSel srcsel_1 (.reg1(out_4), .reg2(out_6), .reg3(out_7), .sel(Rd), .reg0(out_3), .regOut(selRd));
  srcSel srcsel_2 (.reg1(out_4), .reg2(out_6), .reg3(out_7), .sel(Rs), .reg0(out_3), .regOut(selRs));
  instructionDecoder instructiondecoder_1 (
    .IR(instructionRegister_q), .sum(sum), .clk(clk), .rst(rst), .jumpEnable(jumpEnable), .rW(rW),
    .halt(halt), .jumpTarg(jumpTarg), .opCode(op), .Rs(Rs), .Rd(Rd), .sub(sub));
  CSBasedAddSubtract csbasedaddsubtract_1 (.OP(sub), .A(selRd), .B(selRs), .Sum(sum), .Overflow(overflow));
  Multiplexer #(.width(16)) multiplexer_1 (.in0(sum), .in1(selRs), .out(multiplexer_1_out), .sel(op[2]));
  Multiplexer #(.width(16)) multiplexer_2 (.in0({{14{1'b0}}, Rs}), .in1(ld), .out(multiplexer_2_out), .sel(op[0]));
  Multiplexer #(.width(16)) multiplexer_3 (
    .in0(multiplexer_1_out), .in1(multiplexer_2_out), .out(out_2), .sel(and_2_out));
  and and_2 (and_2_out, op[1], op[2], op[3]);
  regWE regwe_1 (
    .Rd(Rd), .regWrite(rW), .reg0WE(regwe_1_reg0we), .reg1WE(regwe_1_reg1we), .reg2WE(regwe_1_reg2we),
    .reg3WE(regwe_1_reg3we));
  Register #(.width(16)) R0 (.D(out_2), .en(regwe_1_reg0we), .clk(clk), .Q(out_3), .clr(rst));
  Register #(.width(16)) R1 (.D(out_2), .en(regwe_1_reg1we), .clk(clk), .Q(out_4), .clr(rst));
  Register #(.width(16)) R2 (.D(out_2), .en(regwe_1_reg2we), .clk(clk), .Q(out_6), .clr(rst));
  Register #(.width(16)) R3 (.D(out_2), .en(regwe_1_reg3we), .clk(clk), .Q(out_7), .clr(rst));
  Register #(.width(1)) register_1 (.D(1'b1), .en(and_3_out), .clk(clk), .Q(register_1_q), .clr(rst));
  and and_3 (and_3_out, and_4_out, overflow);
  and and_4 (and_4_out, ~op[3], ~op[2], op[1]);  // AND_Gate
  LED led_1 (.in(register_1_q));

  // Other names for the same wires on the sheet: R0[15:0] = out_3; R1[15:0] = out_4; R2[15:0] = out_6;
  //   R3[15:0] = out_7

  // Notes on the sheet:
  //   Data
  //   Arithmetic
  //   Instructions
  //   jump enable and targ trigger during decode, not execute
  //   mv
  //   ldi
  //   Registers
endmodule

module regWE (
  input  regWrite,
  input  [1:0] Rd,
  output reg0WE,
  output reg1WE,
  output reg2WE,
  output reg3WE
);

  wire and_1_out, and_2_out, and_3_out, nor_1_out, not_1_out, not_2_out;

  not not_1 (not_1_out, Rd[1]);
  not not_2 (not_2_out, Rd[0]);
  nor nor_1 (nor_1_out, Rd[0], Rd[1]);
  and and_1 (and_1_out, Rd[0], not_1_out);
  and and_2 (and_2_out, not_2_out, Rd[1]);
  and and_3 (and_3_out, Rd[0], Rd[1]);
  and and_4 (reg0WE, nor_1_out, regWrite);
  and and_5 (reg1WE, and_1_out, regWrite);
  and and_6 (reg2WE, and_2_out, regWrite);
  and and_7 (reg3WE, and_3_out, regWrite);
endmodule

module srcSel (
  input  [1:0] sel,
  input  [15:0] reg0,
  input  [15:0] reg1,
  input  [15:0] reg2,
  input  [15:0] reg3,
  output [15:0] regOut
);

  Multiplexer #(.select(2), .width(16)) multiplexer_1 (
    .in0(reg0), .in1(reg1), .in2(reg2), .in3(reg3), .out(regOut), .sel(sel));
endmodule

module programCounter (
  input  [5:0] jumpTarg,
  input  jumpEnable,
  input  clk,
  input  rst,
  output [5:0] pc
);

  wire adder_1_cout, undriven;
  wire [5:0] adder_1_out, multiplexer_1_out;

  // NoConnect on undriven
  Adder #(.width(6)) adder_1 (.a(pc), .b(6'b000001), .out(adder_1_out), .cin(undriven), .cout(adder_1_cout));
  // NoConnect on adder_1_cout
  Register #(.width(6)) register_1 (.D(multiplexer_1_out), .en(1'b1), .clk(clk), .Q(pc), .clr(rst));
  Multiplexer #(.width(6)) multiplexer_1 (.in0(adder_1_out), .in1(jumpTarg), .out(multiplexer_1_out), .sel(jumpEnable));
endmodule

module instructionDecoder (
  input  [7:0] IR,
  input  [15:0] sum,
  input  clk,
  input  rst,
  output sub,
  output rW,
  output halt,
  output jumpEnable,
  output [5:0] jumpTarg,
  output [3:0] opCode,
  output [1:0] Rs,
  output [1:0] Rd
);

  wire and_1_out, and_2_out, and_3_out, and_4_out, and_5_out, and_6_out, and_7_out, and_8_out, and_9_out,
       fv_q, not_1_out, or_1_out;

  not not_1 (not_1_out, IR[1]);
  and and_1 (and_1_out, IR[2], IR[1]);
  and and_2 (and_2_out, ~IR[3], ~IR[2], IR[1]);  // AND_Gate
  and and_3 (and_3_out, ~IR[3], and_1_out, ~IR[0]);  // AND_Gate
  and and_4 (and_4_out, IR[4], IR[5]);
  and and_5 (and_5_out, IR[6], IR[7]);
  and and_6 (and_6_out, ~IR[0], not_1_out);  // AND_Gate
  D_Flip_Flop fv (.D(1'b1), .clk(clk), .Q(fv_q), .reset(rst));  // open: Qn, preset
  or or_1 (or_1_out, and_1_out, and_2_out);
  and and_7 (and_7_out, and_3_out, and_4_out, and_5_out);
  or or_2 (jumpEnable, and_9_out, and_8_out);
  and and_8 (and_8_out, and_6_out, fv_q);
  and and_9 (and_9_out, sum[15], IR[0], not_1_out);
  D_Flip_Flop d_ff_1 (.D(IR[0]), .clk(clk), .Q(sub), .reset(rst));  // open: Qn, preset
  D_Flip_Flop d_ff_2 (.D(or_1_out), .clk(clk), .Q(rW), .reset(rst));  // open: Qn, preset
  D_Flip_Flop d_ff_3 (.D(and_7_out), .clk(clk), .Q(halt), .reset(rst));  // open: Qn, preset
  Register #(.width(4)) register_1 (.D(IR[3:0]), .en(1'b1), .clk(clk), .Q(opCode), .clr(rst));
  Register #(.width(2)) register_2 (.D(IR[5:4]), .en(1'b1), .clk(clk), .Q(Rs), .clr(rst));
  Register #(.width(2)) register_3 (.D(IR[7:6]), .en(1'b1), .clk(clk), .Q(Rd), .clr(rst));

  assign jumpTarg = IR[7:2];
endmodule

module cycleCounter (
  input  halt,
  input  clk,
  input  rst,
  output [15:0] out_4
);

  wire not_1_out, register_1_q;

  Register #(.width(1)) register_1 (.D(1'b1), .en(halt), .clk(clk), .Q(register_1_q), .clr(rst));
  not not_1 (not_1_out, register_1_q);
  Counter #(.max('hffff), .width(16)) counter_1 (
    .count(not_1_out), .Q(out_4), .clk(clk), .clr(rst));  // open: load, D, carry, up
endmodule
