// Logisim project Multiplexers.circ as structural Verilog: 6 circuits, main circuit Mux2to1Logic
module Mux2to1Logic (
  input  in0,
  input  s,
  input  in1,
  output z
);

  wire nand_1_out, nand_2_out, not_1_out;

  not not_1 (not_1_out, s);
  nand nand_1 (nand_1_out, in0, not_1_out);
  nand nand_2 (nand_2_out, in1, s);
  nand nand_3 (z, nand_1_out, nand_2_out);

  // Notes on the sheet:
  //   14 transistors
  //   2 to 1 Multiplexer
  //   Saffron Liu
  //   max(s + 2.75, in0 + 2, in1 + 2)
endmodule

module Mux4to1Logic (
  input  in0,
  input  in1,
  input  in2,
  input  in3,
  input  s0,
  input  s1,
  output out_7
);

  wire mux2to1logic_1_z, mux2to1logic_2_z;

  Mux2to1Logic mux2to1logic_1 (.in1(in1), .in0(in0), .s(s0), .z(mux2to1logic_1_z));
  Mux2to1Logic mux2to1logic_2 (.in1(in3), .in0(in2), .s(s0), .z(mux2to1logic_2_z));
  Mux2to1Logic mux2to1logic_3 (.in1(mux2to1logic_2_z), .in0(mux2to1logic_1_z), .s(s1), .z(out_7));

  // Notes on the sheet:
  //   42 transistors
  //   Saffron Liu
  //   4 to 1 Multiplexer
  //   max(s0 + 4.75, s1 + 2.75, in0 + 4, in1 + 4, in2 + 4, in3 + 4)
endmodule

module Mux2to1Transmission (
  input  in0,
  input  in1,
  input  s,
  output out_4
);

  wire transmission_1_p3, transmission_1_p4;

  // Transmission_Gate transmission_1: pin names not known; wires that end beside it: in0, s, transmission_1_p3, transmission_1_p4
  not not_1 (transmission_1_p3, s);
  // Transmission_Gate transmission_2: pin names not known; wires that end beside it: in1, transmission_1_p3, s, transmission_1_p4
  not not_2 (out_4, transmission_1_p4);

  // Notes on the sheet:
  //   8 transistors
  //   2 to 1 Multiplexer
  //   Saffron Liu
  //   max(s + 1.75, in0 + 1, in1 + 1)
endmodule

module Mux4to1Transmission (
  input  in0,
  input  in1,
  input  in2,
  input  in3,
  input  s0,
  input  s1,
  output out_7
);

  wire mux2to1transmission_1_out_4, mux2to1transmission_3_out_4;

  Mux2to1Transmission mux2to1transmission_1 (.in1(in1), .s(s0), .in0(in0), .out_4(mux2to1transmission_1_out_4));
  Mux2to1Transmission mux2to1transmission_2 (
    .in1(mux2to1transmission_3_out_4), .s(s1), .in0(mux2to1transmission_1_out_4), .out_4(out_7));
  Mux2to1Transmission mux2to1transmission_3 (.in1(in3), .s(s0), .in0(in2), .out_4(mux2to1transmission_3_out_4));

  // Notes on the sheet:
  //   24 transistors
  //   4 to 1 Multiplexer
  //   Saffron Liu
  //   max(s0 + 2.75, s1 + 1.75, in0 + 2, in1 + 2, in2 + 2, in3 + 2)
endmodule

module Mux2to1Inv_4Bit (
  input  [3:0] A,
  input  [3:0] B,
  input  Cin,
  output [3:0] out_4
);

  Mux2to1Transmission mux2to1transmission_1 (.in1(B[0]), .s(Cin), .in0(A[0]), .out_4(out_4[0]));
  Mux2to1Transmission mux2to1transmission_2 (.in1(B[1]), .s(Cin), .in0(A[1]), .out_4(out_4[1]));
  Mux2to1Transmission mux2to1transmission_3 (.in1(B[2]), .s(Cin), .in0(A[2]), .out_4(out_4[2]));
  Mux2to1Transmission mux2to1transmission_4 (.in1(B[3]), .s(Cin), .in0(A[3]), .out_4(out_4[3]));
endmodule

module Mux2to1Inv_8Bit (
  input  [7:0] A,
  input  Cin,
  input  [7:0] B,
  output [7:0] out_4
);

  Mux2to1Inv_4Bit mux2to1inv_4bit_1 (.Cin(Cin), .A(A[7:4]), .B(B[7:4]), .out_4(out_4[7:4]));
  Mux2to1Inv_4Bit mux2to1inv_4bit_2 (.Cin(Cin), .A(A[3:0]), .B(B[3:0]), .out_4(out_4[3:0]));
endmodule
