// Logisim project Overflow.circ as structural Verilog: 1 circuit, main circuit main
module main (
  input  A3,
  input  B3,
  input  R3,
  input  OP,
  output Overflow
);

  wire and_1_out, and_2_out, multiplexer_1_out, nor_1_out, nor_2_out, nor_3_out, not_1_out, or_1_out;

  Multiplexer multiplexer_1 (.in0(B3), .in1(not_1_out), .out(multiplexer_1_out), .sel(OP));
  not not_1 (not_1_out, B3);
  nor nor_1 (nor_1_out, multiplexer_1_out, A3);
  and and_1 (and_1_out, multiplexer_1_out, A3);
  nor nor_2 (nor_2_out, A3, R3);
  and and_2 (and_2_out, A3, R3);
  or or_1 (or_1_out, nor_1_out, and_1_out);
  nor nor_3 (nor_3_out, nor_2_out, and_2_out);
  and and_3 (Overflow, or_1_out, nor_3_out);
endmodule
